# Fritzing sketch OpenSensor (saved by Fritzing 1.0.4)

parts:
  A1 = ESP32-S3-WROOM-1-N16R8 dev board
  M1 = ph-4502c [package=THT]
  Part1 = ADS1115
  OLED_I2C1 = OLED 128x64 I2C Monochrome Display
  A2 = tds-sensor-meter-v1.0_1
  DS1 = DS18B20 1-Wire Temperature Sensor Probe
  A3 = Arduino pluggable terminal
  L298N1 = L298N DC motor driver
  L298N2 = L298N DC motor driver
  M2 = DC Motor [voltage_(max)=6V voltage_(min)=3V]
  M3 = DC Motor [voltage_(max)=6V voltage_(min)=3V]
  M4 = DC Motor [voltage_(max)=6V voltage_(min)=3V]
  M5 = DC Motor [voltage_(max)=6V voltage_(min)=3V]

nets:
  N1: A1.Pin_1, A1.Pin_2, A2.pin2
  N2: A1.Pin_12, Part1.SDA, OLED_I2C1.SDA
  N3: A1.Pin_15, Part1.SCL, OLED_I2C1.SCK
  VDD: A1.Pin_21, M1.pin6, Part1.VDD, OLED_I2C1.VDD, DS1.VDD, A3.Pin_2, A3.Pin_5, L298N1.5V, L298N2.5V
  GND: A1.Pin_22, A1.Pin_44, M1.pin4, M1.pin5, Part1.GND, OLED_I2C1.GND, A2.pin3, DS1.GND, A3.Pin_3, A3.Pin_4, L298N1.GND, L298N2.GND
  N4: A1.Pin_32, L298N1.IN1
  N5: A1.Pin_33, L298N1.IN2
  N6: A1.Pin_34, L298N1.IN3
  N7: A1.Pin_35, L298N1.IN4
  N8: A1.Pin_36, L298N2.IN1
  N9: A1.Pin_37, L298N2.IN2
  N10: A1.Pin_38, L298N2.IN3
  N11: A1.Pin_39, L298N2.IN4
  N12: A1.Pin_40, A2.pin1
  N13: A1.Pin_41, DS1.DQ, A3.Pin_1, A3.Pin_6
  N14: M1.pin3, Part1.A0
  N15: L298N1.OUT1, M2.pin_1
  N16: L298N1.OUT2, M2.pin_2
  N17: L298N1.OUT3, M3.pin_2
  N18: L298N1.OUT4, M3.pin_1
  N19: L298N2.OUT1, M4.pin_1
  N20: L298N2.OUT2, M4.pin_2
  N21: L298N2.OUT3, M5.pin_2
  N22: L298N2.OUT4, M5.pin_1

notes:
  SDA
  SCL

custom parts:
  ESP32-S3-WROOM-1-N16R8 dev board: ESP32-S3 WIFI+BLE5.0 Development Board ESP32-S3-WROOM-1-N16R8(16M Flash/8SRAM).
  ph-4502c: ph-4502c PH Meter.
  ADS1115: ADC ADS1115
  : TDS Meter V1.0 Development Board Water Meter Filter Measuring Water Sensor Module.
  Arduino pluggable terminal: Arduino pluggable terminal.
  L298N DC motor driver: 2x DC motor driver with 78M05 positive voltage regulator (7..35 V) L298N: max 46 V, 2 A Set 5 V Enable jumper to enable 5 V regultor (needed for the L298N) and +5 V output at screw terminal or supply external +5 V at screw terminal Set ENA and/or ENB to +5 V to enable motor permanently or supply ENA and/or ENB with PWM signal IN1 and IN2 set rotation directory for motor A (OUT1/OUT2) IN2 and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

// code stored in the sketch: old.ino
#static const uint8_t SDA = 8;
#static const uint8_t SCL = 9;
